# Fritzing sketch wiring-diagram (saved by Fritzing 0.9.3b)

parts:
  Raspberry_Pi1 = Raspberry Pi 2
  U1 = 2-Channel 5v Relay Shield [package=relay-2ch5v10a]
  S1 = Round Pushbutton
  U2 = Vibration Motor- ROB-08449 [package=vibe-motor-10mm]
  S4 = Magnetic Door Switch [package=reed_switch_plastic]

nets:
  N1: Raspberry_Pi1.GPIO4, U1.IN1
  N2: Raspberry_Pi1.GPIO18, S4.2
  GND: Raspberry_Pi1.GND, U1.GND
  5V: Raspberry_Pi1.5V, U1.VCC, S4.1
  N3: U1.K1-In, S1.leg0, U2.+
  N4: U1.K1-On, S1.leg1, U2.-

custom parts:
  2-Channel 5v Relay Shield: 2 Channel 5v Relay Shield w. 2x SPD-06VDC-SD-C
